// Logisim project CPU.circ as structural Verilog: 2 circuits, main circuit main
module main (
);

  Timer timer_1 ();  // open: Increment, Clock, Clear, T0, T1, T2, T3, T4, T5, T6, T7, T8, T9, T10, T11, T12, T13, T14, T15, Overflow
endmodule

module Timer (
  input  Increment,
  input  Clock,
  input  Clear,
  output T0,
  output T1,
  output T2,
  output T3,
  output T4,
  output T5,
  output T6,
  output T7,
  output T8,
  output T9,
  output T10,
  output T11,
  output T12,
  output T13,
  output T14,
  output T15,
  output Overflow
);

  wire [3:0] counter_1_q;

  Counter #(.width(4), .max('hf)) counter_1 (
    .count(Increment), .Q(counter_1_q), .carry(Overflow), .clk(Clock), .clr(Clear));  // open: load, D
  Decoder #(.select(4)) decoder_1 (
    .out0(T0), .out1(T1), .out2(T2), .out3(T3), .out4(T4), .out5(T5), .out6(T6), .out7(T7), .out8(T8),
    .out9(T9), .out10(T10), .out11(T11), .out12(T12), .out13(T13), .out14(T14), .out15(T15), .sel(counter_1_q));  // open: en
endmodule
